// Logisim project d8_new.circ as structural Verilog: 35 circuits, main circuit main
module main (
  input  AU_CE_L,
  input  GPR_CE_L,
  input  AU_U_DL,
  input  GPR_U_DL,
  input  AU_LOAD_L,
  input  GPR_LOAD_L,
  input  AU_LOAD_TH,
  input  GPR_OE_L,
  input  AU_LOAD_TL,
  input  GPR_WE_L,
  input  [2:0] AU_R_N,
  input  [1:0] GRP_R_N,
  input  [2:0] AU_W_N,
  input  [1:0] GRP_W_N,
  input  CR_OE_L,
  input  CR_LOAD_L,
  input  CR_LOAD_H,
  input  in_18
);

  wire address_unit_1_p11, clock_1_out, ic_xx02_1_y1, ic_xx02_1_y4, pipeline_1_skip;
  wire [7:0] address_unit_1_p2, dipswitch_1_sw1;
  wire [15:0] CR_q;

  Clock clock_1 (.out(clock_1_out));
  IC_xx02 ic_xx02_1 (
    .Y1(ic_xx02_1_y1), .A1(clock_1_out), .B1(clock_1_out), .Y4(ic_xx02_1_y4), .B4(pipeline_1_skip),
    .A4(ic_xx02_1_y1));  // open: Y2, A2, B2, Y3, B3, A3
  pipeline pipeline_1 (
    .CLK(clock_1_out), .SKIP(pipeline_1_skip));  // open: D, LOAD_M, FLAGS, CYCLE, CTRL0, CTRL1, CTRL2, CTRL3
  constant_register CR (.D(address_unit_1_p2), .LOAD_CONST_LOW(CR_LOAD_L), .LOAD_CONST_HIGH(CR_LOAD_H), .Q(CR_q));
  DipSwitch dipswitch_1 (
    .sw1(dipswitch_1_sw1[0]), .sw2(dipswitch_1_sw1[1]), .sw3(dipswitch_1_sw1[2]), .sw4(dipswitch_1_sw1[3]),
    .sw5(dipswitch_1_sw1[4]), .sw6(dipswitch_1_sw1[5]), .sw7(dipswitch_1_sw1[6]), .sw8(dipswitch_1_sw1[7]));
  // address_unit address_unit_1: pin names not known; wires that end beside it: ic_xx02_1_y4, address_unit_1_p2, CR_q, AU_W_N, AU_R_N, AU_LOAD_TL, AU_LOAD_TH, AU_LOAD_L, AU_U_DL, AU_CE_L, address_unit_1_p11
  IC_xx540 ic_xx540_1 (.OE1_L(CR_OE_L), .D(CR_q[7:0]), .OE2_L(1'b0), .Q(address_unit_1_p2));
  IC_xx540 ic_xx540_2 (.OE1_L(in_18), .D(dipswitch_1_sw1), .OE2_L(in_18), .Q(address_unit_1_p2));
  gpr_unit gpr_unit_1 (
    .Q(address_unit_1_p2), .CLK(ic_xx02_1_y4), .W_N(GRP_W_N), .GPR_WE_L(GPR_WE_L), .data(address_unit_1_p2),
    .U_DL(GPR_U_DL), .CE_L(GPR_CE_L), .LOAD_L(GPR_LOAD_L), .R_N(GRP_R_N), .GPR_OE_L(GPR_OE_L));
  // LedBar #(.inputtype("row"), .matrixcols(16)) ledbar_1: pin names not known; wires that end beside it: address_unit_1_p11
  // LedBar #(.inputtype("row")) ledbar_2: pin names not known; wires that end beside it: address_unit_1_p2

  // Notes on the sheet:
  //   ASSERT CR MAIN BUS #
endmodule

module address_unit (
  input  [2:0] W_N,
  input  [2:0] R_N,
  input  CLK,
  input  LOAD_TL,
  input  LOAD_TH,
  input  [7:0] D,
  input  PC_CE_L,
  input  SP_U_DL,
  input  SP_CE_L,
  input  RA_CE_L,
  input  SI_U_DL,
  input  SI_CE_L,
  input  DI_U_DL,
  input  DI_CE_L,
  input  [15:0] const16,
  output [15:0] A
);

  wire ic_xx02_1_y1, ic_xx02_1_y2, ic_xx02_1_y4, ic_xx04_1_y2, ic_xx04_1_y5, READ_y1_l, READ_y2_l, READ_y3_l,
       READ_y4_l, READ_y5_l, READ_y6_l, READ_y7_l, WRITE_y1_l, WRITE_y2_l, WRITE_y3_l, WRITE_y4_l,
       WRITE_y5_l, WRITE_y7_l;
  wire [7:0] th_q, tl_q;
  wire [15:0] di_out_8, il_reg16_1_out_8, pc_out_8, si_out_8, sp_out_8;

  IC_xx04 ic_xx04_1 (
    .A2(LOAD_TL), .A5(LOAD_TH), .Y2(ic_xx04_1_y2), .Y5(ic_xx04_1_y5));  // open: A1, A3, A4, A6, Y1, Y3, Y4, Y6
  IC_xx02 ic_xx02_1 (
    .Y1(ic_xx02_1_y1), .A1(LOAD_TL), .B1(ic_xx02_1_y4), .Y2(ic_xx02_1_y2), .A2(LOAD_TH), .B2(ic_xx02_1_y4),
    .Y4(ic_xx02_1_y4), .B4(WRITE_y7_l), .A4(WRITE_y7_l));  // open: Y3, B3, A3
  IC_xx540 ic_xx540_1 (.OE1_L(ic_xx04_1_y2), .D(D), .OE2_L(1'b0), .Q(A[7:0]));
  IC_xx540 ic_xx540_2 (.OE1_L(ic_xx04_1_y5), .D(D), .OE2_L(1'b0), .Q(A[15:8]));
  IC_xx540 ic_xx540_3 (.OE1_L(1'b0), .D(const16[7:0]), .OE2_L(READ_y6_l), .Q(A[7:0]));
  IC_xx540 ic_xx540_4 (.OE1_L(1'b0), .D(const16[15:8]), .OE2_L(READ_y6_l), .Q(A[15:8]));
  l_reg8 tl (.D(A[7:0]), .CLK(CLK), .LOAD_L(ic_xx02_1_y1), .Q(tl_q));  // open: NC_U_DL, NC_CE2_L, NC_CE1_L, CO_L
  IC_xx540 ic_xx540_5 (.OE1_L(1'b0), .D(tl_q), .OE2_L(READ_y7_l), .Q(A[7:0]));
  l_reg8 th (.D(A[15:8]), .CLK(CLK), .LOAD_L(ic_xx02_1_y2), .Q(th_q));  // open: NC_U_DL, NC_CE2_L, NC_CE1_L, CO_L
  IC_xx540 ic_xx540_6 (.OE1_L(1'b0), .D(th_q), .OE2_L(READ_y7_l), .Q(A[15:8]));
  IC_xx138 WRITE (
    .SEL(W_N), .EN1_L(1'b0), .EN2_L(1'b0), .EN3(CLK), .Y1_L(WRITE_y1_l), .Y2_L(WRITE_y2_l),
    .Y3_L(WRITE_y3_l), .Y4_L(WRITE_y4_l), .Y5_L(WRITE_y5_l), .Y7_L(WRITE_y7_l));  // open: Y0_L, Y6_L
  il_reg16 pc (
    .D(A), .CLK(CLK), .CE2_L(1'b0), .LOAD_L(WRITE_y1_l), .CE1_L(PC_CE_L), .out_8(pc_out_8));  // open: NC_U_DL, CO_L
  dil_reg16 sp (
    .D(A), .CLK(CLK), .U_DL(SP_U_DL), .CE2_L(1'b0), .LOAD_L(WRITE_y2_l), .CE1_L(SP_CE_L), .out_8(sp_out_8));  // open: CO_L
  il_reg16 il_reg16_1 (
    .D(A), .CLK(CLK), .CE2_L(1'b0), .LOAD_L(WRITE_y3_l), .CE1_L(RA_CE_L), .out_8(il_reg16_1_out_8));  // open: NC_U_DL, CO_L
  dil_reg16 si (
    .D(A), .CLK(CLK), .U_DL(SI_U_DL), .CE2_L(1'b0), .LOAD_L(WRITE_y4_l), .CE1_L(SI_CE_L), .out_8(si_out_8));  // open: CO_L
  dil_reg16 di (
    .D(A), .CLK(CLK), .U_DL(DI_U_DL), .CE2_L(1'b0), .LOAD_L(WRITE_y5_l), .CE1_L(DI_CE_L), .out_8(di_out_8));  // open: CO_L
  IC_xx540 ic_xx540_7 (.OE1_L(1'b0), .D(pc_out_8[7:0]), .OE2_L(READ_y1_l), .Q(A[7:0]));
  IC_xx540 ic_xx540_8 (.OE1_L(1'b0), .D(pc_out_8[15:8]), .OE2_L(READ_y1_l), .Q(A[15:8]));
  IC_xx540 ic_xx540_9 (.OE1_L(1'b0), .D(sp_out_8[7:0]), .OE2_L(READ_y2_l), .Q(A[7:0]));
  IC_xx540 ic_xx540_10 (.OE1_L(1'b0), .D(sp_out_8[15:8]), .OE2_L(READ_y2_l), .Q(A[15:8]));
  IC_xx540 ic_xx540_11 (.OE1_L(1'b0), .D(il_reg16_1_out_8[7:0]), .OE2_L(READ_y3_l), .Q(A[7:0]));
  IC_xx540 ic_xx540_12 (.OE1_L(1'b0), .D(il_reg16_1_out_8[15:8]), .OE2_L(READ_y3_l), .Q(A[15:8]));
  IC_xx540 ic_xx540_13 (.OE1_L(1'b0), .D(si_out_8[7:0]), .OE2_L(READ_y4_l), .Q(A[7:0]));
  IC_xx540 ic_xx540_14 (.OE1_L(1'b0), .D(si_out_8[15:8]), .OE2_L(READ_y4_l), .Q(A[15:8]));
  IC_xx540 ic_xx540_15 (.OE1_L(1'b0), .D(di_out_8[7:0]), .OE2_L(READ_y5_l), .Q(A[7:0]));
  IC_xx540 ic_xx540_16 (.OE1_L(1'b0), .D(di_out_8[15:8]), .OE2_L(READ_y5_l), .Q(A[15:8]));
  IC_xx138 READ (
    .SEL(R_N), .EN1_L(1'b0), .EN2_L(1'b0), .EN3(1'b1), .Y1_L(READ_y1_l), .Y2_L(READ_y2_l), .Y3_L(READ_y3_l),
    .Y4_L(READ_y4_l), .Y5_L(READ_y5_l), .Y6_L(READ_y6_l), .Y7_L(READ_y7_l));  // open: Y0_L
endmodule

module constant_register (
  input  [7:0] D,
  input  LOAD_CONST_LOW,
  input  LOAD_CONST_HIGH,
  output [15:0] Q
);

  IC_xx574 const_low (.OE_L(1'b0), .D(D), .O(Q[7:0]), .CP(LOAD_CONST_LOW));
  IC_xx574 const_high (.OE_L(1'b0), .D(D), .O(Q[15:8]), .CP(LOAD_CONST_HIGH));
endmodule

module ctrl0 (
  input  [1:0] CYCLE,
  input  [15:0] BITS,
  output [7:0] CTRL
);

  ROM #(.addrWidth(18)) rom_1 (.addr({BITS, CYCLE}), .data(CTRL));

  // Notes on the sheet:
  //   SST39SF020A
endmodule

module ctrl1 (
  input  [1:0] CYCLE,
  input  [15:0] BITS,
  output [7:0] CTRL
);

  ROM #(.addrWidth(18)) rom_1 (.addr({BITS, CYCLE}), .data(CTRL));

  // Notes on the sheet:
  //   SST39SF020A
endmodule

module ctrl2 (
  input  [1:0] CYCLE,
  input  [15:0] BITS,
  output [7:0] CTRL
);

  ROM #(.addrWidth(18)) rom_1 (.addr({BITS, CYCLE}), .data(CTRL));

  // Notes on the sheet:
  //   SST39SF020A
endmodule

module ctrl3 (
  input  [1:0] CYCLE,
  input  [15:0] BITS,
  output [7:0] CTRL
);

  ROM #(.addrWidth(18)) rom_1 (.addr({BITS, CYCLE}), .data(CTRL));

  // Notes on the sheet:
  //   SST39SF020A
endmodule

module gpr_unit (
  input  [1:0] W_N,
  input  [1:0] R_N,
  input  GPR_OE_L,
  input  GPR_WE_L,
  input  CLK,
  input  [7:0] data,
  input  U_DL,
  input  CE_L,
  input  LOAD_L,
  output [7:0] Q
);

  wire ic_xx02_1_y1, ic_xx02_1_y2, ic_xx02_1_y4, ic_xx04_1_y3, ic_xx04_1_y4, ic_xx04_1_y5, ic_xx04_1_y6,
       ic_xx139_1_y10_l, ic_xx139_1_y20_l, ic_xx139_1_y21_l, ic_xx139_1_y22_l, ic_xx139_1_y23_l,
       ic_xx139_1_y_11_l, ic_xx139_1_y_12_l, ic_xx139_1_y_13_l;
  wire [7:0] a_q, b_q, c_q, d_q;

  IC_xx02 ic_xx02_1 (
    .Y1(ic_xx02_1_y1), .A1(GPR_WE_L), .B1(ic_xx02_1_y2), .Y2(ic_xx02_1_y2), .A2(CLK), .B2(CLK),
    .Y4(ic_xx02_1_y4), .B4(ic_xx02_1_y1), .A4(ic_xx02_1_y1));  // open: Y3, B3, A3
  IC_xx04 ic_xx04_1 (
    .A3(ic_xx139_1_y_13_l), .A4(ic_xx139_1_y_12_l), .A5(ic_xx139_1_y_11_l), .A6(ic_xx139_1_y10_l),
    .Y3(ic_xx04_1_y3), .Y4(ic_xx04_1_y4), .Y5(ic_xx04_1_y5), .Y6(ic_xx04_1_y6));  // open: A1, A2, Y1, Y2
  dil_reg8 a (
    .D(data), .CLK(ic_xx04_1_y6), .U_DL(U_DL), .CE2_L(CE_L), .LOAD_L(LOAD_L), .CE1_L(1'b0), .Q(a_q));  // open: CO_L
  dil_reg8 b (
    .D(data), .CLK(ic_xx04_1_y5), .U_DL(U_DL), .CE2_L(CE_L), .LOAD_L(LOAD_L), .CE1_L(1'b0), .Q(b_q));  // open: CO_L
  dil_reg8 c (
    .D(data), .CLK(ic_xx04_1_y4), .U_DL(U_DL), .CE2_L(CE_L), .LOAD_L(LOAD_L), .CE1_L(1'b0), .Q(c_q));  // open: CO_L
  dil_reg8 d (
    .D(data), .CLK(ic_xx04_1_y3), .U_DL(U_DL), .CE2_L(CE_L), .LOAD_L(LOAD_L), .CE1_L(1'b0), .Q(d_q));  // open: CO_L
  IC_xx139 ic_xx139_1 (
    .EN_1_L(ic_xx02_1_y4), .SEL_1(W_N), .Y10_L(ic_xx139_1_y10_l), .Y_11_L(ic_xx139_1_y_11_l),
    .Y_12_L(ic_xx139_1_y_12_l), .Y_13_L(ic_xx139_1_y_13_l), .EN_2_L(GPR_OE_L), .SEL_2(R_N),
    .Y20_L(ic_xx139_1_y20_l), .Y21_L(ic_xx139_1_y21_l), .Y22_L(ic_xx139_1_y22_l), .Y23_L(ic_xx139_1_y23_l));
  IC_xx540 ic_xx540_1 (.OE1_L(1'b0), .D(a_q), .OE2_L(ic_xx139_1_y20_l), .Q(Q));
  IC_xx540 ic_xx540_2 (.OE1_L(1'b0), .D(b_q), .OE2_L(ic_xx139_1_y21_l), .Q(Q));
  IC_xx540 ic_xx540_3 (.OE1_L(1'b0), .D(c_q), .OE2_L(ic_xx139_1_y22_l), .Q(Q));
  IC_xx540 ic_xx540_4 (.OE1_L(1'b0), .D(d_q), .OE2_L(ic_xx139_1_y23_l), .Q(Q));
endmodule

module pipeline (
  input  CLK,
  input  [7:0] D,
  input  LOAD_M,
  input  [3:0] FLAGS,
  output [1:0] CYCLE,
  output SKIP,
  output [15:0] CTRL0,
  output [15:0] CTRL1,
  output [15:0] CTRL2,
  output [15:0] CTRL3
);

  wire ic_xx02_1_y1, ic_xx02_1_y2, ic_xx02_1_y4, transistor_1_out;
  wire [3:3] ic_xx163_1_q;
  wire [7:0] ic_xx174_1_q0;
  wire [7:4] ic_xx574_2_o, ic_xx574_4_o, ic_xx574_5_o, ic_xx574_7_o, ic_xx574_8_o, ic_xx574_10_o,
       ic_xx574_11_o, undriven;

  Transistor #(.\type ("n")) transistor_1 (.in(1'b0), .out(transistor_1_out), .gate(SKIP));
  Pull_Resistor #(.pull(1)) pull_resistor_1 (.node(transistor_1_out));
  IC_xx163 ic_xx163_1 (
    .CLR_L(transistor_1_out), .CLK(CLK), .ENP(1'b1), .Q({ic_xx163_1_q[3], SKIP, CYCLE}), .ENT(1'b1),
    .LOAD_L(1'b1));  // open: D, RCO
  IC_xx02 ic_xx02_1 (
    .Y1(ic_xx02_1_y1), .A1(ic_xx02_1_y2), .B1(ic_xx02_1_y2), .Y2(ic_xx02_1_y2), .A2(CYCLE[0]), .B2(CYCLE[1]),
    .Y4(ic_xx02_1_y4), .B4(ic_xx02_1_y1), .A4(SKIP));  // open: Y3, B3, A3
  IC_xx574 ic_xx574_1 (.OE_L(1'b0), .D(D), .O(CTRL0[7:0]), .CP(SKIP));
  IC_xx174 ic_xx174_1 (
    .MR(ic_xx02_1_y4), .D0(D[0]), .D1(D[1]), .D2(D[2]), .D3(D[3]), .Q0(ic_xx174_1_q0[0]),
    .Q1(ic_xx174_1_q0[1]), .Q2(ic_xx174_1_q0[2]), .Q3(ic_xx174_1_q0[3]), .CP(LOAD_M));  // open: D4, D5, Q4, Q5
  IC_xx574 ic_xx574_2 (.OE_L(1'b0), .D({undriven, FLAGS}), .O({ic_xx574_2_o, CTRL0[15:12]}), .CP(SKIP));
  IC_xx574 ic_xx574_3 (.OE_L(1'b0), .D(CTRL0[7:0]), .O(CTRL1[7:0]), .CP(SKIP));
  IC_xx574 ic_xx574_4 (.OE_L(1'b0), .D(ic_xx174_1_q0), .O({ic_xx574_4_o, CTRL1[11:8]}), .CP(SKIP));
  IC_xx574 ic_xx574_5 (.OE_L(1'b0), .D({ic_xx574_2_o, CTRL0[15:12]}), .O({ic_xx574_5_o, CTRL1[15:12]}), .CP(SKIP));
  IC_xx574 ic_xx574_6 (.OE_L(1'b0), .D(CTRL1[7:0]), .O(CTRL2[7:0]), .CP(SKIP));
  IC_xx574 ic_xx574_7 (.OE_L(1'b0), .D({ic_xx574_4_o, CTRL1[11:8]}), .O({ic_xx574_7_o, CTRL2[11:8]}), .CP(SKIP));
  IC_xx574 ic_xx574_8 (.OE_L(1'b0), .D({ic_xx574_5_o, CTRL1[15:12]}), .O({ic_xx574_8_o, CTRL2[15:12]}), .CP(SKIP));
  IC_xx574 ic_xx574_9 (.OE_L(1'b0), .D(CTRL2[7:0]), .O(CTRL3[7:0]), .CP(SKIP));
  IC_xx574 ic_xx574_10 (.OE_L(1'b0), .D({ic_xx574_7_o, CTRL2[11:8]}), .O({ic_xx574_10_o, CTRL3[11:8]}), .CP(SKIP));
  IC_xx574 ic_xx574_11 (.OE_L(1'b0), .D({ic_xx574_8_o, CTRL2[15:12]}), .O({ic_xx574_11_o, CTRL3[15:12]}), .CP(SKIP));
  // LedBar #(.inputtype("row"), .matrixcols(16)) ledbar_1: pin names not known; wires that end beside it: {CTRL0[15:12], 4'b0000, CTRL0[7:0]}
  // LedBar #(.inputtype("row"), .matrixcols(16)) ledbar_2: pin names not known; wires that end beside it: CTRL1
  // LedBar #(.inputtype("row"), .matrixcols(16)) ledbar_3: pin names not known; wires that end beside it: CTRL2
  // LedBar #(.inputtype("row"), .matrixcols(16)) ledbar_4: pin names not known; wires that end beside it: CTRL3

  assign CTRL0[11:8] = 4'b0000;
endmodule

// +-L8
module dil_reg8 (
  input  [7:0] D,
  input  CLK,
  input  U_DL,
  input  CE2_L,
  input  LOAD_L,
  input  CE1_L,
  output CO_L,
  output [7:0] Q
);

  wire ic_xx169_1_rco_l;

  IC_xx169 ic_xx169_1 (
    .U_DL(U_DL), .D(D[3:0]), .ENP_L(CE2_L), .CLK(CLK), .RCO_L(ic_xx169_1_rco_l), .Q(Q[3:0]), .ENT_L(CE1_L),
    .LOAD_L(LOAD_L));
  IC_xx169 ic_xx169_2 (
    .U_DL(U_DL), .D(D[7:4]), .ENP_L(ic_xx169_1_rco_l), .CLK(CLK), .RCO_L(CO_L), .Q(Q[7:4]), .ENT_L(CE1_L),
    .LOAD_L(LOAD_L));
endmodule

// L8
module l_reg8 (
  input  [7:0] D,
  input  CLK,
  input  NC_U_DL,
  input  NC_CE2_L,
  input  LOAD_L,
  input  NC_CE1_L,
  output CO_L,
  output [7:0] Q
);

  wire ic_xx169_1_rco_l;

  IC_xx169 ic_xx169_1 (
    .U_DL(1'b1), .D(D[3:0]), .ENP_L(1'b1), .CLK(CLK), .RCO_L(ic_xx169_1_rco_l), .Q(Q[3:0]), .ENT_L(1'b1),
    .LOAD_L(LOAD_L));
  IC_xx169 ic_xx169_2 (
    .U_DL(1'b1), .D(D[7:4]), .ENP_L(ic_xx169_1_rco_l), .CLK(CLK), .RCO_L(CO_L), .Q(Q[7:4]), .ENT_L(1'b1),
    .LOAD_L(LOAD_L));
endmodule

// +-16
module di_reg16 (
  input  [15:0] D,
  input  CLK,
  input  U_DL,
  input  CE2_L,
  input  NC_LOAD_L,
  input  CE1_L,
  output CO_L,
  output [15:0] out_8
);

  wire ic_xx169_1_rco_l, ic_xx169_2_rco_l, ic_xx169_3_rco_l, pull_resistor_1_node;

  Pull_Resistor #(.pull(1)) pull_resistor_1 (.node(pull_resistor_1_node));
  IC_xx169 ic_xx169_1 (
    .U_DL(U_DL), .D(D[3:0]), .ENP_L(CE2_L), .CLK(CLK), .RCO_L(ic_xx169_1_rco_l), .Q(out_8[3:0]),
    .ENT_L(CE1_L), .LOAD_L(pull_resistor_1_node));
  IC_xx169 ic_xx169_2 (
    .U_DL(U_DL), .D(D[7:4]), .ENP_L(ic_xx169_1_rco_l), .CLK(CLK), .RCO_L(ic_xx169_2_rco_l), .Q(out_8[7:4]),
    .ENT_L(CE1_L), .LOAD_L(pull_resistor_1_node));
  IC_xx169 ic_xx169_3 (
    .U_DL(U_DL), .D(D[11:8]), .ENP_L(ic_xx169_2_rco_l), .CLK(CLK), .RCO_L(ic_xx169_3_rco_l), .Q(out_8[11:8]),
    .ENT_L(CE1_L), .LOAD_L(pull_resistor_1_node));
  IC_xx169 ic_xx169_4 (
    .U_DL(U_DL), .D(D[15:12]), .ENP_L(ic_xx169_3_rco_l), .CLK(CLK), .RCO_L(CO_L), .Q(out_8[15:12]),
    .ENT_L(CE1_L), .LOAD_L(pull_resistor_1_node));
endmodule

// +-L16
module dil_reg16 (
  input  [15:0] D,
  input  CLK,
  input  U_DL,
  input  CE2_L,
  input  LOAD_L,
  input  CE1_L,
  output CO_L,
  output [15:0] out_8
);

  wire ic_xx169_1_rco_l, ic_xx169_2_rco_l, ic_xx169_3_rco_l;

  IC_xx169 ic_xx169_1 (
    .U_DL(U_DL), .D(D[3:0]), .ENP_L(CE2_L), .CLK(CLK), .RCO_L(ic_xx169_1_rco_l), .Q(out_8[3:0]),
    .ENT_L(CE1_L), .LOAD_L(LOAD_L));
  IC_xx169 ic_xx169_2 (
    .U_DL(U_DL), .D(D[7:4]), .ENP_L(ic_xx169_1_rco_l), .CLK(CLK), .RCO_L(ic_xx169_2_rco_l), .Q(out_8[7:4]),
    .ENT_L(CE1_L), .LOAD_L(LOAD_L));
  IC_xx169 ic_xx169_3 (
    .U_DL(U_DL), .D(D[11:8]), .ENP_L(ic_xx169_2_rco_l), .CLK(CLK), .RCO_L(ic_xx169_3_rco_l), .Q(out_8[11:8]),
    .ENT_L(CE1_L), .LOAD_L(LOAD_L));
  IC_xx169 ic_xx169_4 (
    .U_DL(U_DL), .D(D[15:12]), .ENP_L(ic_xx169_3_rco_l), .CLK(CLK), .RCO_L(CO_L), .Q(out_8[15:12]),
    .ENT_L(CE1_L), .LOAD_L(LOAD_L));
endmodule

// +L16
module il_reg16 (
  input  [15:0] D,
  input  CLK,
  input  NC_U_DL,
  input  CE2_L,
  input  LOAD_L,
  input  CE1_L,
  output CO_L,
  output [15:0] out_8
);

  wire ic_xx169_1_rco_l, ic_xx169_2_rco_l, ic_xx169_3_rco_l;

  IC_xx169 ic_xx169_1 (
    .U_DL(1'b1), .D(D[3:0]), .ENP_L(CE2_L), .CLK(CLK), .RCO_L(ic_xx169_1_rco_l), .Q(out_8[3:0]),
    .ENT_L(CE1_L), .LOAD_L(LOAD_L));
  IC_xx169 ic_xx169_2 (
    .U_DL(1'b1), .D(D[7:4]), .ENP_L(ic_xx169_1_rco_l), .CLK(CLK), .RCO_L(ic_xx169_2_rco_l), .Q(out_8[7:4]),
    .ENT_L(CE1_L), .LOAD_L(LOAD_L));
  IC_xx169 ic_xx169_3 (
    .U_DL(1'b1), .D(D[11:8]), .ENP_L(ic_xx169_2_rco_l), .CLK(CLK), .RCO_L(ic_xx169_3_rco_l), .Q(out_8[11:8]),
    .ENT_L(CE1_L), .LOAD_L(LOAD_L));
  IC_xx169 ic_xx169_4 (
    .U_DL(1'b1), .D(D[15:12]), .ENP_L(ic_xx169_3_rco_l), .CLK(CLK), .RCO_L(CO_L), .Q(out_8[15:12]),
    .ENT_L(CE1_L), .LOAD_L(LOAD_L));
endmodule

// L16
module l_reg16 (
  input  [15:0] D,
  input  CLK,
  input  NC_U_DL,
  input  NC_CE2_L,
  input  LOAD_L,
  input  NC_CE1_L,
  output CO_L,
  output [15:0] out_8
);

  wire ic_xx169_1_rco_l, ic_xx169_2_rco_l, ic_xx169_3_rco_l;

  IC_xx169 ic_xx169_1 (
    .U_DL(1'b1), .D(D[3:0]), .ENP_L(1'b1), .CLK(CLK), .RCO_L(ic_xx169_1_rco_l), .Q(out_8[3:0]), .ENT_L(1'b1),
    .LOAD_L(LOAD_L));
  IC_xx169 ic_xx169_2 (
    .U_DL(1'b1), .D(D[7:4]), .ENP_L(ic_xx169_1_rco_l), .CLK(CLK), .RCO_L(ic_xx169_2_rco_l), .Q(out_8[7:4]),
    .ENT_L(1'b1), .LOAD_L(LOAD_L));
  IC_xx169 ic_xx169_3 (
    .U_DL(1'b1), .D(D[11:8]), .ENP_L(ic_xx169_2_rco_l), .CLK(CLK), .RCO_L(ic_xx169_3_rco_l), .Q(out_8[11:8]),
    .ENT_L(1'b1), .LOAD_L(LOAD_L));
  IC_xx169 ic_xx169_4 (
    .U_DL(1'b1), .D(D[15:12]), .ENP_L(ic_xx169_3_rco_l), .CLK(CLK), .RCO_L(CO_L), .Q(out_8[15:12]),
    .ENT_L(1'b1), .LOAD_L(LOAD_L));
endmodule

// xx02
module DIP_xx02 (
  input  Vcc,
  input  A1,
  input  B1,
  input  B4,
  input  A4,
  input  A2,
  input  B2,
  input  B3,
  input  GND,
  input  A3,
  output Y1,
  output Y4,
  output Y2,
  output Y3
);

  nor nor_1 (Y1, A1, B1);
  nor nor_2 (Y2, A2, B2);
  nor nor_3 (Y4, A4, B4);
  nor nor_4 (Y3, A3, B3);

  // Notes on the sheet:
  //   A4: pull=up
  //   B3: pull=up
  //   Vcc: pull=up
  //   B4: pull=up
  //   A2: pull=up
  //   A1: pull=up
  //   B1: pull=up
endmodule

// xx04
module DIP_xx04 (
  input  A1,
  input  Vcc,
  input  A6,
  input  A2,
  input  A5,
  input  A3,
  input  A4,
  input  GND,
  output Y1,
  output Y6,
  output Y2,
  output Y5,
  output Y3,
  output Y4
);

  not not_1 (Y1, A1);
  not not_2 (Y6, A6);
  not not_3 (Y2, A2);
  not not_4 (Y5, A5);
  not not_5 (Y3, A3);
  not not_6 (Y4, A4);

  // Notes on the sheet:
  //   A5: pull=up
  //   A4: pull=up
  //   Vcc: pull=up
  //   A6: pull=up
  //   A3: pull=up
  //   A1: pull=up
  //   A2: pull=up
endmodule

module DIP_xx138 (
  input  A,
  input  Vcc,
  input  B,
  input  C,
  input  EN1_L,
  input  EN2_L,
  input  EN3,
  input  GND,
  output Y0_L,
  output Y1_L,
  output Y2_L,
  output Y3_L,
  output Y4_L,
  output Y7_L,
  output Y5_L,
  output Y6_L
);

  wire or_2_out;

  or or_1 (Y7_L, ~C, ~B, ~A, or_2_out);  // OR_Gate
  or or_2 (or_2_out, EN1_L, EN2_L, ~EN3);  // OR_Gate
  or or_3 (Y0_L, C, B, A, or_2_out);
  or or_4 (Y1_L, ~C, B, A, or_2_out);  // OR_Gate
  or or_5 (Y2_L, C, ~B, A, or_2_out);  // OR_Gate
  or or_6 (Y3_L, ~C, ~B, A, or_2_out);  // OR_Gate
  or or_7 (Y4_L, C, B, ~A, or_2_out);  // OR_Gate
  or or_8 (Y5_L, ~C, B, ~A, or_2_out);  // OR_Gate
  or or_9 (Y6_L, C, ~B, ~A, or_2_out);  // OR_Gate

  // Notes on the sheet:
  //   C: pull=up
  //   EN1_L: pull=up
  //   EN2_L: pull=up
  //   EN3: pull=up
  //   A: pull=up
  //   B: pull=up
endmodule

// xx139
module DIP_xx139 (
  input  EN1_L,
  input  Vcc,
  input  A1,
  input  EN2_L,
  input  B1,
  input  A2,
  input  B2,
  input  GND,
  output Y10_L,
  output Y11_L,
  output Y20_L,
  output Y12_L,
  output Y21_L,
  output Y13_L,
  output Y22_L,
  output Y23_L
);

  or or_1 (Y10_L, B1, A1, EN1_L);
  or or_2 (Y11_L, ~B1, A1, EN1_L);  // OR_Gate
  or or_3 (Y12_L, B1, ~A1, EN1_L);  // OR_Gate
  or or_4 (Y13_L, ~B1, ~A1, EN1_L);  // OR_Gate
  or or_5 (Y20_L, B2, A2, EN2_L);
  or or_6 (Y21_L, ~B2, A2, EN2_L);  // OR_Gate
  or or_7 (Y22_L, B2, ~A2, EN2_L);  // OR_Gate
  or or_8 (Y23_L, ~B2, ~A2, EN2_L);  // OR_Gate

  // Notes on the sheet:
  //   B1: pull=up
  //   EN1_L: pull=up
  //   A1: pull=up
  //   A2: pull=up
  //   B2: pull=up
  //   EN2_L: pull=up
endmodule

// xx163
module DIP_xx163 (
  input  CLR_L,
  input  Vcc,
  input  CLK,
  input  A,
  input  B,
  input  C,
  input  D,
  input  ENP,
  input  ENT,
  input  GND,
  input  LOAD_L,
  output RCO,
  output Q_A,
  output Q_B,
  output Q_C,
  output Q_D
);

  _74163 u_74163_1 (
    .pin1(CLR_L), .pin2(CLK), .pin3(A), .pin4(B), .pin5(C), .pin6(D), .pin7(ENP), .pin15(RCO), .pin14(Q_A),
    .pin13(Q_B), .pin12(Q_C), .pin11(Q_D), .pin10(ENT), .pin9(LOAD_L));
endmodule

module DIP_xx169 (
  input  U_DL,
  input  Vcc,
  input  CLK,
  input  A,
  input  B,
  input  C,
  input  D,
  input  ENP_L,
  input  ENT_L,
  input  GND,
  input  LOAD_L,
  output RCO_L,
  output Q_A,
  output Q_B,
  output Q_C,
  output Q_D
);

  wire counter_1_carry, nor_1_out, not_1_out;

  Counter #(.max('hf), .width(4)) counter_1 (
    .load(not_1_out), .D({D, C, B, A}), .count(nor_1_out), .Q({Q_D, Q_C, Q_B, Q_A}), .carry(counter_1_carry),
    .up(U_DL), .clk(CLK), .clr(1'b0));
  nor nor_1 (nor_1_out, ENP_L, ENT_L);
  not not_1 (not_1_out, LOAD_L);
  not not_2 (RCO_L, counter_1_carry);
endmodule

// xx174
module DIP_xx174 (
  input  MR,
  input  Vcc,
  input  D0,
  input  D5,
  input  D1,
  input  D4,
  input  D2,
  input  D3,
  input  GND,
  input  CP,
  output Q0,
  output Q5,
  output Q1,
  output Q4,
  output Q2,
  output Q3
);

  D_Flip_Flop d_ff_1 (.clk(CP), .D(D0), .Q(Q0), .preset(1'b0), .reset(MR));  // open: Qn
  D_Flip_Flop d_ff_2 (.clk(CP), .D(D1), .Q(Q1), .preset(1'b0), .reset(MR));  // open: Qn
  D_Flip_Flop d_ff_3 (.clk(CP), .D(D2), .Q(Q2), .preset(1'b0), .reset(MR));  // open: Qn
  D_Flip_Flop d_ff_4 (.clk(CP), .D(D5), .Q(Q5), .preset(1'b0), .reset(MR));  // open: Qn
  D_Flip_Flop d_ff_5 (.clk(CP), .D(D4), .Q(Q4), .preset(1'b0), .reset(MR));  // open: Qn
  D_Flip_Flop d_ff_6 (.clk(CP), .D(D3), .Q(Q3), .preset(1'b0), .reset(MR));  // open: Qn
endmodule

// xx193
module DIP_xx193 (
  input  B,
  input  Vcc,
  input  A,
  input  CLR,
  input  DOWN,
  input  UP,
  input  LOAD_L,
  input  C,
  input  GND,
  input  D,
  output Q_B,
  output Q_A,
  output BO_L,
  output CO_L,
  output Q_C,
  output Q_D
);

  wire and_1_out, and_2_out, and_3_out, and_4_out, and_5_out, and_6_out, and_7_out, and_8_out, and_9_out,
       and_10_out, and_11_out, and_12_out, and_13_out, and_14_out, and_15_out, and_16_out, not_1_out,
       not_2_out, not_3_out, not_4_out, not_5_out, not_6_out, not_7_out, not_8_out, not_11_out, not_12_out,
       not_13_out, not_14_out, not_15_out, not_16_out, not_17_out, not_18_out, not_19_out, or_1_out,
       or_2_out, or_3_out, or_4_out, or_5_out, or_6_out, or_7_out, or_8_out, t_ff_1_qn, t_ff_2_qn, t_ff_3_qn,
       t_ff_4_qn;

  not not_1 (not_1_out, DOWN);
  not not_2 (not_2_out, UP);
  not not_3 (not_3_out, LOAD_L);
  not not_4 (not_4_out, CLR);
  and and_1 (and_1_out, not_2_out, Q_A);
  and and_2 (and_2_out, t_ff_1_qn, not_1_out);
  and and_3 (and_3_out, not_2_out, Q_B, Q_A);
  and and_4 (and_4_out, t_ff_1_qn, t_ff_2_qn, not_1_out);
  and and_5 (and_5_out, not_2_out, Q_C, Q_B, Q_A);
  and and_6 (and_6_out, t_ff_1_qn, t_ff_2_qn, t_ff_3_qn, not_1_out);
  or or_1 (or_1_out, not_2_out, not_1_out);
  not not_5 (not_5_out, or_1_out);
  or or_2 (or_2_out, and_1_out, and_2_out);
  not not_6 (not_6_out, or_2_out);
  or or_3 (or_3_out, and_3_out, and_4_out);
  not not_7 (not_7_out, or_3_out);
  or or_4 (or_4_out, and_5_out, and_6_out);
  not not_8 (not_8_out, or_4_out);
  and and_7 (and_7_out, A, not_3_out, not_4_out);
  and and_8 (and_8_out, B, not_3_out, not_4_out);
  and and_9 (and_9_out, C, not_3_out, not_4_out);
  and and_10 (and_10_out, D, not_3_out, not_4_out);
  and and_11 (and_11_out, t_ff_1_qn, t_ff_2_qn, t_ff_3_qn, t_ff_4_qn, not_1_out);
  not not_9 (BO_L, and_11_out);
  and and_12 (and_12_out, Q_A, Q_B, Q_C, Q_D, not_2_out);
  not not_10 (CO_L, and_12_out);
  not not_11 (not_11_out, and_7_out);
  not not_12 (not_12_out, and_8_out);
  not not_13 (not_13_out, and_9_out);
  not not_14 (not_14_out, and_10_out);
  not not_15 (not_15_out, not_4_out);
  or or_5 (or_5_out, and_13_out, not_15_out);
  and and_13 (and_13_out, not_3_out, not_11_out);
  not not_16 (not_16_out, not_11_out);
  or or_6 (or_6_out, and_14_out, not_15_out);
  and and_14 (and_14_out, not_3_out, not_12_out);
  not not_17 (not_17_out, not_12_out);
  or or_7 (or_7_out, and_15_out, not_15_out);
  and and_15 (and_15_out, not_3_out, not_13_out);
  not not_18 (not_18_out, not_13_out);
  or or_8 (or_8_out, and_16_out, not_15_out);
  and and_16 (and_16_out, not_3_out, not_14_out);
  not not_19 (not_19_out, not_14_out);
  T_Flip_Flop t_ff_1 (.clk(not_5_out), .T(1'b1), .Q(Q_A), .Qn(t_ff_1_qn), .preset(not_16_out), .reset(or_5_out));
  T_Flip_Flop t_ff_2 (.clk(not_6_out), .T(1'b1), .Q(Q_B), .Qn(t_ff_2_qn), .preset(not_17_out), .reset(or_6_out));
  T_Flip_Flop t_ff_3 (.clk(not_7_out), .T(1'b1), .Q(Q_C), .Qn(t_ff_3_qn), .preset(not_18_out), .reset(or_7_out));
  T_Flip_Flop t_ff_4 (.clk(not_8_out), .T(1'b1), .Q(Q_D), .Qn(t_ff_4_qn), .preset(not_19_out), .reset(or_8_out));

  // Notes on the sheet:
  //   C: pull=up
  //   D: pull=up
  //   A: pull=up
  //   CLR: pull=up
  //   DOWN: pull=up
  //   UP: pull=up
  //   B: pull=up
endmodule

// xx540
module DIP_xx540 (
  input  OE1_L,
  input  Vcc,
  input  D0,
  input  OE2_L,
  input  D1,
  input  D2,
  input  D3,
  input  D4,
  input  D5,
  input  D6,
  input  D7,
  input  GND,
  output Q0,
  output Q1,
  output Q2,
  output Q3,
  output Q4,
  output Q5,
  output Q6,
  output Q7
);

  wire and_1_out, not_1_out, not_2_out;

  not not_1 (not_1_out, OE1_L);
  and and_1 (and_1_out, not_1_out, not_2_out);
  not not_2 (not_2_out, OE2_L);
  assign Q0 = and_1_out ? D0 : 1'bz;  // Controlled_Buffer controlled_buffer_1
  assign Q1 = and_1_out ? D1 : 1'bz;  // Controlled_Buffer controlled_buffer_2
  assign Q2 = and_1_out ? D2 : 1'bz;  // Controlled_Buffer controlled_buffer_3
  assign Q3 = and_1_out ? D3 : 1'bz;  // Controlled_Buffer controlled_buffer_4
  assign Q4 = and_1_out ? D4 : 1'bz;  // Controlled_Buffer controlled_buffer_5
  assign Q5 = and_1_out ? D5 : 1'bz;  // Controlled_Buffer controlled_buffer_6
  assign Q6 = and_1_out ? D6 : 1'bz;  // Controlled_Buffer controlled_buffer_7
  assign Q7 = and_1_out ? D7 : 1'bz;  // Controlled_Buffer controlled_buffer_8

  // Notes on the sheet:
  //   D2: pull=up
  //   D3: pull=up
  //   D4: pull=up
  //   D5: pull=up
  //   D6: pull=up
  //   D7: pull=up
  //   OE1_L: pull=up
  //   D0: pull=up
  //   D1: pull=up
  //   OE2_L: pull=up
endmodule

// xx574
module DIP_xx574 (
  input  OE_L,
  input  Vcc,
  input  D0,
  input  D1,
  input  D2,
  input  D3,
  input  D4,
  input  D5,
  input  D6,
  input  D7,
  input  GND,
  input  CP,
  output Q0,
  output Q1,
  output Q2,
  output Q3,
  output Q4,
  output Q5,
  output Q6,
  output Q7
);

  wire not_1_out;
  wire [7:0] register_1_q;

  not not_1 (not_1_out, OE_L);
  Register register_1 (.D({D7, D6, D5, D4, D3, D2, D1, D0}), .en(1'b1), .Q(register_1_q), .clk(CP), .clr(1'b0));
  assign {Q7, Q6, Q5, Q4, Q3, Q2, Q1, Q0} = not_1_out ? register_1_q : 8'bz;  // Controlled_Buffer controlled_buffer_1

  // Notes on the sheet:
  //   D1: pull=up
  //   D2: pull=up
  //   D3: pull=up
  //   D4: pull=up
  //   D5: pull=up
  //   D6: pull=up
  //   D7: pull=up
  //   OE_L: pull=up
  //   D0: pull=up
  //   CP: pull=up
endmodule

// xx02
module IC_xx02 (
  input  A1,
  input  B4,
  input  B1,
  input  A4,
  input  A2,
  input  B3,
  input  B2,
  input  A3,
  output Y1,
  output Y4,
  output Y2,
  output Y3
);

  DIP_xx02 dip_xx02_1 (
    .Y1(Y1), .A1(A1), .B1(B1), .Y2(Y2), .A2(A2), .B2(B2), .Y4(Y4), .B4(B4), .A4(A4), .Y3(Y3), .B3(B3), .A3(A3));  // open: GND, Vcc

  // Notes on the sheet:
  //   A1: pull=up
  //   B1: pull=up
  //   A2: pull=up
  //   B4: pull=up
  //   A4: pull=up
  //   B3: pull=up
endmodule

// xx04
module IC_xx04 (
  input  A1,
  input  A2,
  input  A3,
  input  A4,
  input  A5,
  input  A6,
  output Y1,
  output Y2,
  output Y3,
  output Y4,
  output Y5,
  output Y6
);

  DIP_xx04 dip_xx04_1 (
    .A1(A1), .Y1(Y1), .A2(A2), .Y2(Y2), .A3(A3), .Y3(Y3), .A6(A4), .Y6(Y4), .A5(A5), .Y5(Y5), .A4(A6), .Y4(Y6));  // open: GND, Vcc

  // Notes on the sheet:
  //   A1: pull=up
  //   A2: pull=up
  //   A3: pull=up
  //   A4: pull=up
  //   A5: pull=up
  //   A6: pull=up
endmodule

// xx138
module IC_xx138 (
  input  [2:0] SEL,
  input  EN1_L,
  input  EN2_L,
  input  EN3,
  output Y0_L,
  output Y1_L,
  output Y2_L,
  output Y3_L,
  output Y4_L,
  output Y5_L,
  output Y6_L,
  output Y7_L
);

  DIP_xx138 dip_xx138_1 (
    .A(SEL[2]), .B(SEL[1]), .C(SEL[0]), .EN1_L(EN1_L), .EN2_L(EN2_L), .EN3(EN3), .Y7_L(Y7_L), .Y0_L(Y0_L),
    .Y1_L(Y1_L), .Y2_L(Y2_L), .Y3_L(Y3_L), .Y4_L(Y4_L), .Y5_L(Y5_L), .Y6_L(Y6_L));  // open: GND, Vcc
endmodule

// xx139
module IC_xx139 (
  input  EN_1_L,
  input  EN_2_L,
  input  [1:0] SEL_1,
  input  [1:0] SEL_2,
  output Y10_L,
  output Y20_L,
  output Y_11_L,
  output Y21_L,
  output Y_12_L,
  output Y22_L,
  output Y_13_L,
  output Y23_L
);

  DIP_xx139 dip_xx139_1 (
    .EN1_L(EN_1_L), .A1(SEL_1[1]), .B1(SEL_1[0]), .Y10_L(Y10_L), .Y11_L(Y_11_L), .Y12_L(Y_12_L),
    .Y13_L(Y_13_L), .EN2_L(EN_2_L), .A2(SEL_2[1]), .B2(SEL_2[0]), .Y20_L(Y20_L), .Y21_L(Y21_L),
    .Y22_L(Y22_L), .Y23_L(Y23_L));  // open: GND, Vcc
endmodule

// 163
module IC_xx163 (
  input  CLR_L,
  input  CLK,
  input  [3:0] D,
  input  ENP,
  input  ENT,
  input  LOAD_L,
  output RCO,
  output [3:0] Q
);

  DIP_xx163 dip_xx163_1 (
    .CLR_L(CLR_L), .CLK(CLK), .A(D[0]), .B(D[1]), .C(D[2]), .D(D[3]), .ENP(ENP), .RCO(RCO), .Q_A(Q[0]),
    .Q_B(Q[1]), .Q_C(Q[2]), .Q_D(Q[3]), .ENT(ENT), .LOAD_L(LOAD_L));  // open: GND, Vcc
endmodule

// 169
module IC_xx169 (
  input  U_DL,
  input  [3:0] D,
  input  ENP_L,
  input  ENT_L,
  input  LOAD_L,
  input  CLK,
  output RCO_L,
  output [3:0] Q
);

  wire counter_1_carry, nor_1_out, not_1_out;

  Counter #(.max('hf), .width(4)) counter_1 (
    .load(not_1_out), .D(D), .count(nor_1_out), .Q(Q), .carry(counter_1_carry), .up(U_DL), .clk(CLK),
    .clr(1'b0));
  nor nor_1 (nor_1_out, ENP_L, ENT_L);
  not not_1 (not_1_out, LOAD_L);
  not not_2 (RCO_L, counter_1_carry);
endmodule

// xx174
module IC_xx174 (
  input  MR,
  input  D0,
  input  D1,
  input  D2,
  input  D3,
  input  D4,
  input  D5,
  input  CP,
  output Q0,
  output Q1,
  output Q2,
  output Q3,
  output Q4,
  output Q5
);

  DIP_xx174 dip_xx174_1 (
    .MR(MR), .Q0(Q0), .D0(D0), .D1(D1), .Q1(Q1), .D2(D2), .Q2(Q2), .Q5(Q5), .D5(D5), .D4(D4), .Q4(Q4),
    .D3(D3), .Q3(Q3), .CP(CP));  // open: GND, Vcc
endmodule

// 193
module IC_xx193 (
  input  [3:0] D,
  input  LOAD_L,
  input  CLR,
  input  DOWN,
  input  UP,
  output [3:0] Q,
  output BO_L,
  output CO_L
);

  DIP_xx193 dip_xx193_1 (
    .B(D[1]), .Q_B(Q[1]), .Q_A(Q[0]), .DOWN(DOWN), .UP(UP), .Q_C(Q[2]), .Q_D(Q[3]), .A(D[0]), .CLR(CLR),
    .BO_L(BO_L), .CO_L(CO_L), .LOAD_L(LOAD_L), .C(D[2]), .D(D[3]));  // open: GND, Vcc
endmodule

// 540
module IC_xx540 (
  input  OE1_L,
  input  OE2_L,
  input  [7:0] D,
  output [7:0] Q
);

  DIP_xx540 dip_xx540_1 (
    .OE1_L(OE1_L), .D0(D[0]), .D1(D[1]), .D2(D[2]), .D3(D[3]), .D4(D[4]), .D5(D[5]), .D6(D[6]), .D7(D[7]),
    .OE2_L(OE2_L), .Q0(Q[0]), .Q1(Q[1]), .Q2(Q[2]), .Q3(Q[3]), .Q4(Q[4]), .Q5(Q[5]), .Q6(Q[6]), .Q7(Q[7]));  // open: GND, Vcc
endmodule

// 574
module IC_xx574 (
  input  OE_L,
  input  [7:0] D,
  input  CP,
  output [7:0] O
);

  DIP_xx574 dip_xx574_1 (
    .OE_L(OE_L), .D0(D[0]), .D1(D[1]), .D2(D[2]), .D3(D[3]), .D4(D[4]), .D5(D[5]), .D6(D[6]), .D7(D[7]),
    .Q0(O[0]), .Q1(O[1]), .Q2(O[2]), .Q3(O[3]), .Q4(O[4]), .Q5(O[5]), .Q6(O[6]), .Q7(O[7]), .CP(CP));  // open: GND, Vcc

  // Notes on the sheet:
  //   OE_L: pull=up
  //   D: pull=up
  //   CP: pull=up
endmodule
